# Fritzing sketch Overall (saved by Fritzing 0.8.7b)
breadboards: 1

parts:
  ARDUINO = Arduino Mega ADK (Rev3)
  IR1 = TSOP312.., 314.. [part_number=TSOP31240 package=THT]
  IR2 = TSOP312.., 314.. [part_number=TSOP31240 package=THT]
  IR3 = TSOP312.., 314.. [part_number=TSOP31240 package=THT]
  IR4 = TSOP312.., 314.. [part_number=TSOP31240 package=THT]
  IR5 = TSOP312.., 314.. [part_number=TSOP31240 package=THT]
  IR6 = TSOP312.., 314.. [part_number=TSOP31240 package=THT]
  IR7 = TSOP312.., 314.. [part_number=TSOP31240 package=THT]
  IR8 = TSOP312.., 314.. [part_number=TSOP31240 package=THT]
  IR9 = TSOP312.., 314.. [part_number=TSOP31240 package=THT]
  IR10 = TSOP312.., 314.. [part_number=TSOP31240 package=THT]
  IR11 = TSOP312.., 314.. [part_number=TSOP31240 package=THT]
  IR12 = TSOP312.., 314.. [part_number=TSOP31240 package=THT]
  IR13 = TSOP312.., 314.. [part_number=TSOP31240 package=THT]
  IR14 = TSOP312.., 314.. [part_number=TSOP31240 package=THT]
  IR15 = TSOP312.., 314.. [part_number=TSOP31240 package=THT]

nets:
  GND: ARDUINO.GND, IR1.GND, IR2.GND, IR3.GND, IR4.GND, IR5.GND, IR6.GND, IR7.GND, IR8.GND, IR9.GND, IR10.GND, IR11.GND, IR12.GND, IR13.GND, IR14.GND, IR15.GND
  N1: ARDUINO.IOREF, ARDUINO.5V, IR1.Vs, IR2.Vs, IR3.Vs
